# Fritzing sketch strain_guage (saved by Fritzing 0.9.3b)
breadboards: 2

parts:
  Mod1 = Raspberry Pi Pico
  R1 = Resistor [tolerance=±1% resistance=121 package="1206 [SMD]"]
  R2 = Resistor [tolerance=±1% resistance=121 package="1206 [SMD]"]
  R3 = Resistor [tolerance=±1% resistance=121 package="1206 [SMD]"]
  Strain_Guage_Shield = Arduino Uno (Rev3)
  Strain_Guage_1 = Resistor [tolerance=±1% resistance=121 package="1206 [SMD]"]
  R4 = Resistor [tolerance=±1% resistance=121 package="1206 [SMD]"]
  R5 = Resistor [tolerance=±1% resistance=121 package="1206 [SMD]"]
  Strain_Guage_sheild_Pinout_2 = IC, SIP package, 4 pins [chip_label=Strain]
  Strain_Guage_2 = Resistor [tolerance=±1% resistance=121 package="1206 [SMD]"]
  R6 = Resistor [tolerance=±1% resistance=121 package="1206 [SMD]"]
  Strain_Guage_sheild_Pinout_1 = IC, SIP package, 4 pins [chip_label=Strain]

nets:
  N1: Mod1.pin_23, Mod1.pin_33, Strain_Guage_Shield.GND
  N2: Mod1.pin_31, Strain_Guage_Shield.A0
  N3: Mod1.pin_36, Strain_Guage_Shield.3V3
  5V: Mod1.pin_40, Strain_Guage_Shield.5V, Strain_Guage_Shield.VIN
  N4: R1.Pin_0, R2.Pin_0, Strain_Guage_sheild_Pinout_1.pin1
  N5: R1.Pin_1, Strain_Guage_1.Pin_0, Strain_Guage_sheild_Pinout_1.pin3
  N6: R2.Pin_1, R3.Pin_0, Strain_Guage_sheild_Pinout_1.pin2
  N7: R3.Pin_1, Strain_Guage_1.Pin_1, Strain_Guage_sheild_Pinout_1.pin4
  N8: R4.Pin_0, Strain_Guage_sheild_Pinout_2.pin1, R6.Pin_0
  N9: R4.Pin_1, Strain_Guage_sheild_Pinout_2.pin3, Strain_Guage_2.Pin_0
  N10: R5.Pin_0, Strain_Guage_sheild_Pinout_2.pin2, R6.Pin_1
  N11: R5.Pin_1, Strain_Guage_sheild_Pinout_2.pin4, Strain_Guage_2.Pin_1

custom parts:
  Raspberry Pi Pico: Raspberry Pi Pico. Based around the RP2040 microcontroller the Pico is a low cost microcontroller device bringing Raspberry Pi quality, cost, and easy of use to the microcontroller space. Jan 2021, Split part in to two versions: tht (this one) and SMD. This one will drill holes for a .1 in header in pcb to allow plugging in the module as well as providing pads to solder the module to the top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
